// Logisim project Single_Cycle_Processor.circ as structural Verilog: 3 circuits, main circuit Single_Cycle_Processor
module Single_Cycle_Processor (
);

  wire ALUSrc, B, clock_1_out, Ext, J, MemRd, MemtoReg, MemWr, RegSource, RegWr;
  wire [4:0] ImmL, instruction_spliter_1_rd, instruction_spliter_1_rs1, instruction_spliter_1_rs2,
       multiplexer_2_out;
  wire [5:0] OpCode;
  wire [10:0] Function, ImmH, ImmU;
  wire [15:0] Imm16;
  wire [19:0] ALUControl, BranshPC, JumpPC, PC, pc_1_1_outpcplus1, Register_q;
  wire [31:0] ALUIn, ALUOut, data_memory_1_data_out, Extended, instruction_memory_1__32_bit_iinstruction,
       Output, R1, R2, R3, R4, R5, R6, R7, R8, R9, R10, R11, R12, R13, R14, R15, R16, R17, R18, R19, R20,
       R21, R22, R23, R24, R25, R26, R27, R28, R29, R30, R31, register_file_1_busa, Rs1, Rs2;

  Clock clock_1 (.out(clock_1_out));
  // Probe on R1
  // Probe on R2
  Jump jump_1 (.Imm16(Imm16), .Pc_jump(JumpPC), .Rs1(Rs1));
  Multiplexer #(.select(2), .width(20), .enable("false")) multiplexer_1 (
    .in0(pc_1_1_outpcplus1), .in1(BranshPC), .in2(JumpPC), .in3({20{1'b0}}), .out(PC), .sel({J, B}));
  // Probe on R3
  Register #(.width(20)) Register (.D(PC), .Q(Register_q), .clk(clock_1_out));  // open: en, clr
  // Probe on R4
  PC_1 pc_1_1 (.Initial_Pc(Register_q), .OutPcPlus1(pc_1_1_outpcplus1));
  // Branch_pc branch_pc_1: pin names not known; wires that end beside it: ImmL, ImmH, PC, BranshPC
  // Probe on R5
  // Probe on R6
  // Probe on R7
  ALU_Control alu_control_1 (.Opcode(OpCode), .Function(Function), .ALU_Control(ALUControl));
  // Probe on R8
  Instruction_Memory instruction_memory_1 (
    .PC(Register_q), .Clk(clock_1_out), ._32_bit_iinstruction(instruction_memory_1__32_bit_iinstruction));  // open: Input_Data
  Instruction_Spliter instruction_spliter_1 (
    .in_1(instruction_memory_1__32_bit_iinstruction), .Opcode(OpCode), .RD(instruction_spliter_1_rd),
    .ImmL(ImmL), .Rs1(instruction_spliter_1_rs1), .Rs2(instruction_spliter_1_rs2), .ImmU(ImmU), .F(Function),
    .Imm16(Imm16));
  // Probe on R9
  Multiplexer #(.width(5), .enable("false")) multiplexer_2 (
    .in0(instruction_spliter_1_rs1), .in1(instruction_spliter_1_rd), .out(multiplexer_2_out), .sel(RegSource));
  // Probe on R10
  Control_Signal_Unit control_signal_unit_1 (
    .OP6(OpCode), .out_2(J), .out_3(RegSource), .out_4(RegWr), .out_5(MemRd), .out_6(MemWr),
    .out_7(MemtoReg), .out_8(Ext), .out_9(ALUSrc));
  // Probe on R11
  Register_File register_file_1 (
    .BusW(Output), .RegWrite(RegWr), .R2(R2), .R3(R3), .R4(R4), .R5(R5), .R6(R6), .R7(R7), .R8(R8), .R9(R9),
    .R10(R10), .R11(R11), .R12(R12), .R14(R14), .R15(R15), .R16(R16), .R17(R17), .R18(R18), .R19(R19),
    .R20(R20), .R21(R21), .R22(R22), .R23(R23), .R24(R24), .R25(R25), .R26(R26), .R27(R27), .R28(R28),
    .R29(R29), .R30(R30), .R31(R31), .BusA(register_file_1_busa), .BusB(Rs2), .R1(R1), .R13(R13),
    .Rs1(multiplexer_2_out), .Rs2(instruction_spliter_1_rs2), .Clock(clock_1_out),
    .Rd(instruction_spliter_1_rd));
  // Probe on R12
  // Probe on R13
  // Probe on R14
  // Extender extender_1: pin names not known; wires that end beside it: Imm16, Ext, Extended
  Multiplexer #(.width(32), .enable("false")) multiplexer_3 (.in0(Extended), .in1(Rs2), .out(ALUIn), .sel(ALUSrc));
  // Probe on R15
  // ALU alu_1: pin names not known; wires that end beside it: register_file_1_busa, ALUIn, ALUControl, B, ALUOut
  // Probe on R16
  // Probe on R17
  Data_Memory data_memory_1 (
    .Address(ALUOut), .Data_In(Rs2), .Memory_Write(MemWr), .Clock(clock_1_out),
    .Data_Out(data_memory_1_data_out), .Memory_Read(MemRd));
  // Probe on R18
  Multiplexer #(.width(32), .enable("false")) multiplexer_4 (
    .in0(ALUOut), .in1(data_memory_1_data_out), .out(Output), .sel(MemtoReg));
  // Probe on R19
  // Probe on R20
  // Probe on R21
  // Probe on R22
  // Probe on R23
  // Probe on R24
  // Probe on R25
  // Probe on R26
  // Probe on R27
  // Probe on R28
  // Probe on R29
  // Probe on R30
  // Probe on R31
endmodule

module Instruction_Spliter (
  input  [31:0] in_1,
  output [5:0] Opcode,
  output [4:0] RD,
  output [4:0] ImmL,
  output [4:0] Rs1,
  output [15:0] Imm16,
  output [10:0] F,
  output [10:0] ImmU,
  output [4:0] Rs2
);

  Register #(.width(32)) register_1 (.D(in_1), .Q({F, Imm16[4:0], Rs1, ImmL, Opcode}));  // open: en, clk, clr

  assign Imm16[15:5] = F;
  assign ImmU = F;
  assign RD = ImmL;
  assign Rs2 = Imm16[4:0];

  // Notes on the sheet:
  //   SB_Type
  //   R_Tube
  //   I-Type
endmodule

module temp (
);

  wire ALUSrc, Ext, J, MemRd, MemtoReg, MemWr, RegSource, RegWr;
  wire [5:0] OpCode;

  Storage_Control_Unit storage_control_unit_1 (
    .RegSrc(RegSource), .RegWr(RegWr), .MemRd(MemRd), .MemWr(MemWr), .MemtoReg(MemtoReg), .in_1(OpCode));
  Op_Control op_control_1 (.ExtOp(Ext), .ALUSrc(ALUSrc), ._6_bit_Op(OpCode));
  Pc_Control_Unit pc_control_unit_1 (.in_1(OpCode), .out_3(J));  // open: out_2, out_4
endmodule
